# Fritzing sketch Engin104_fProj_Schematic (saved by Fritzing 0.9.3b)
breadboards: 1

parts:
  Arduino_Uno = Arduino Uno (Rev3)
  G1_-_M1 = Resistor [tolerance=±5% resistance=330 package="0603 [SMD]"]
  G2_-_M2 = Resistor [tolerance=±5% resistance=330 package="0603 [SMD]"]
  G3_-_M4 = Resistor [tolerance=±5% resistance=330 package="0603 [SMD]"]
  G4_-_M8 = Resistor [tolerance=±5% resistance=330 package="0603 [SMD]"]
  G5_-_M16 = Resistor [tolerance=±5% resistance=330 package="0603 [SMD]"]
  G6_-_M32 = Resistor [tolerance=±5% resistance=330 package="0603 [SMD]"]
  LED1 = LED - 5mm [color="Green (570nm)" package="5 mm [THT]"]
  R2-_H2 = Resistor [tolerance=±5% resistance=330 package="0603 [SMD]"]
  R4_-_H8 = Resistor [tolerance=±5% resistance=330 package="0603 [SMD]"]
  R3_-_H4 = Resistor [tolerance=±5% resistance=330 package="0603 [SMD]"]
  R1_-_H1 = Resistor [tolerance=±5% resistance=330 package="0603 [SMD]"]
  LED2 = LED - 5mm [color="Green (570nm)" package="5 mm [THT]"]
  LED3 = LED - 5mm [color="Green (570nm)" package="5 mm [THT]"]
  LED4 = LED - 5mm [color="Green (570nm)" package="5 mm [THT]"]
  LED5 = LED - 5mm [color="Green (570nm)" package="5 mm [THT]"]
  LED6 = LED - 5mm [color="Green (570nm)" package="5 mm [THT]"]
  R1 = LED - 5mm [color="Red (633nm)" package="5 mm [THT]"]
  R2 = LED - 5mm [color="Red (633nm)" package="5 mm [THT]"]
  R3 = LED - 5mm [color="Red (633nm)" package="5 mm [THT]"]
  R4 = LED - 5mm [color="Red (633nm)" package="5 mm [THT]"]
  AM/PM = RGB LED (com. cathode, rgb) [package="5 mm [THT]"]
  ZS-042_RTC1 = ZS-042 RTC Module

nets:
  N1: Arduino_Uno.D8, G6_-_M32.Pin_1
  N2: Arduino_Uno.D9_PWM, G5_-_M16.Pin_1
  N3: Arduino_Uno.D10_PWM/SS, G4_-_M8.Pin_1
  N4: Arduino_Uno.D11_PWM/MOSI, G3_-_M4.Pin_1
  N5: Arduino_Uno.D12/MISO, G2_-_M2.Pin_1
  N6: Arduino_Uno.D13/SCK, G1_-_M1.Pin_1
  GND: Arduino_Uno.GND, LED1.cathode, LED2.cathode, LED3.cathode, LED4.cathode, LED5.cathode, LED6.cathode, R1.cathode, R2.cathode, R3.cathode, R4.cathode, ZS-042_RTC1.GND
  N7: Arduino_Uno.A4/SDA, ZS-042_RTC1.SDA
  N8: Arduino_Uno.A5/SCL, ZS-042_RTC1.SCL
  N9: Arduino_Uno.D2, R1_-_H1.Pin_0
  N10: Arduino_Uno.D3_PWM, R2-_H2.Pin_0
  N11: Arduino_Uno.D4, R3_-_H4.Pin_0
  N12: Arduino_Uno.D5_PWM, R4_-_H8.Pin_0
  N13: Arduino_Uno.D6_PWM, AM/PM.red_anode
  N14: Arduino_Uno.D7, AM/PM.blue_anode
  N15: Arduino_Uno.3V3, AM/PM.common_cathode
  5V: Arduino_Uno.5V, ZS-042_RTC1.VCC
  N16: G1_-_M1.Pin_0, LED1.anode
  N17: G2_-_M2.Pin_0, LED2.anode
  N18: G3_-_M4.Pin_0, LED4.anode
  N19: G4_-_M8.Pin_0, LED3.anode
  N20: G5_-_M16.Pin_0, LED6.anode
  N21: G6_-_M32.Pin_0, LED5.anode
  N22: R2-_H2.Pin_1, R2.anode
  N23: R4_-_H8.Pin_1, R4.anode
  N24: R3_-_H4.Pin_1, R3.anode
  N25: R1_-_H1.Pin_1, R1.anode
